# Fritzing sketch LED_GPIO32-PWM (saved by Fritzing 0.9.3b)
breadboards: 1

parts:
  Tinker_Board1 = Asus Tinker Board [part_number=tinkerBoard-rev1.2]
  R1 = Resistor [tolerance=±5% resistance=220 package=THT]
  LED1 = LED - 5mm [color="Red (633nm)" package="5 mm [THT]"]

nets:
  N1: Tinker_Board1.GPIO32/ASUS239, R1.Pin_1
  N2: Tinker_Board1.GND, LED1.cathode
  N3: R1.Pin_0, LED1.anode

custom parts:
  Asus Tinker Board: The original Asus Tinker Board, a single board computer from Asus. Rockchip RK3288 SoC with 40 GPIO pins.
