# Fritzing sketch photoCell&&cap (saved by Fritzing 0.9.3b)
breadboards: 1

parts:
  Tinker_Board1 = Asus Tinker Board [part_number=tinkerBoard-rev1.2]
  R1 = Photocell (LDR) [package=THT]
  C1 = Electrolytic Capacitor [capacitance=1µF package="100 mil [THT, electrolytic]"]

nets:
  N1: Tinker_Board1.GPIO11/ASUS164, R1.pin_0, C1.+
  N2: Tinker_Board1.GND, C1.-
  N3: Tinker_Board1.5V, R1.pin_1

custom parts:
  Asus Tinker Board: The original Asus Tinker Board, a single board computer from Asus. Rockchip RK3288 SoC with 40 GPIO pins.
